# Fritzing sketch circuit_plan (saved by Fritzing 0.9.3b)
breadboards: 2
stripboards: 1

parts:
  ArduinoMicro = Arduino Micro (Rev3)
  R1 = Resistor [tolerance=±5% resistance=1k package=THT]
  LED1 = LED - 5mm [color="Red (633nm)" package="5 mm [THT]"]
  SW-KB-DISABLE = Toggle Switch [package=THT]
  R2 = Resistor [tolerance=±5% resistance=220 package=THT]
  BoxButton-1 = Square Pushbutton
  BoxButton-2 = Square Pushbutton
  BoxButton-3 = Square Pushbutton
  BoxButton-4 = Square Pushbutton
  R3 = Resistor [tolerance=±5% resistance=2.2k package=THT]
  R4 = Resistor [tolerance=±5% resistance=330 package=THT]
  R5 = Resistor [tolerance=±5% resistance=680 package=THT]
  R6 = Resistor [tolerance=±5% resistance=1k package=THT]
  R7 = Resistor [tolerance=±5% resistance=2.2k package=THT]
  PlayerButton-Q = Arcade Button (white)
  PlayerButton-Qs = Round Pushbutton
  R8 = Resistor [tolerance=±5% resistance=330 package=THT]
  R9 = Resistor [tolerance=±5% resistance=2.2k package=THT]
  PlayerButton-B = Arcade Button (white)
  PlayerButton-Bs = Round Pushbutton
  R10 = Resistor [tolerance=±5% resistance=330 package=THT]
  R11 = Resistor [tolerance=±5% resistance=2.2k package=THT]
  PlayerButton-P = Arcade Button (white)
  PlayerButton-Ps = Round Pushbutton
  R12 = Resistor [tolerance=±5% resistance=330 package=THT]
  BoxButton-Esc = Round Pushbutton
  BoxButton-S = Round Pushbutton
  BoxButton-R = Round Pushbutton
  BoxButton-Q = Round Pushbutton
  BoxButton-N = Round Pushbutton
  BoxButton-Space = Round Pushbutton
  BoxButton-B = Round Pushbutton
  BoxButton-A = Round Pushbutton
  R15 = Resistor [tolerance=±5% resistance=2.2k package=THT]
  R16 = Resistor [tolerance=±5% resistance=330 package=THT]
  R17 = Resistor [tolerance=±5% resistance=680 package=THT]
  R18 = Resistor [tolerance=±5% resistance=1k package=THT]
  R19 = Resistor [tolerance=±5% resistance=3.3k package=THT]
  R20 = Resistor [tolerance=±5% resistance=4.7k package=THT]
  R13 = Resistor [tolerance=±5% resistance=2.2k package=THT]
  R14 = Resistor [tolerance=±5% resistance=330 package=THT]

nets:
  N1: ArduinoMicro.GND, R1.Pin_0, R2.Pin_0, BoxButton-1.leg1, BoxButton-2.leg1, BoxButton-3.leg1, BoxButton-4.leg1, PlayerButton-Q.no_name_yet#1, PlayerButton-Qs.leg1, PlayerButton-B.no_name_yet#1, PlayerButton-Bs.leg1, PlayerButton-P.no_name_yet#1, PlayerButton-Ps.leg1, BoxButton-Esc.leg1, BoxButton-S.leg1, BoxButton-R.leg1, BoxButton-Q.leg1, BoxButton-N.leg1, BoxButton-Space.leg1, BoxButton-B.leg0, BoxButton-A.leg0
  N2: ArduinoMicro.D2/SDA, LED1.anode
  N3: ArduinoMicro.D3/SCL, SW-KB-DISABLE.L2, R2.Pin_1
  N4: ArduinoMicro.5V, SW-KB-DISABLE.COM, R3.Pin_0, R7.Pin_1, R9.Pin_1, R11.Pin_1, R15.Pin_0, R13.Pin_0
  N5: ArduinoMicro.A5, BoxButton-1.leg0, R3.Pin_1, R4.Pin_0
  N6: ArduinoMicro.A4, BoxButton-Esc.leg0, R15.Pin_1, R16.Pin_0
  N7: ArduinoMicro.A3, BoxButton-B.leg1, R13.Pin_1, R14.Pin_0
  N8: ArduinoMicro.A2, R11.Pin_0, PlayerButton-P.no_name_yet#2, R12.Pin_0
  N9: ArduinoMicro.A1, R9.Pin_0, PlayerButton-B.no_name_yet#2, R10.Pin_0
  N10: ArduinoMicro.A0, R7.Pin_0, PlayerButton-Q.no_name_yet#2, R8.Pin_0
  N11: R1.Pin_1, LED1.cathode
  N12: BoxButton-2.leg0, R4.Pin_1, R5.Pin_0
  N13: BoxButton-3.leg0, R5.Pin_1, R6.Pin_0
  N14: BoxButton-4.leg0, R6.Pin_1
  N15: PlayerButton-Qs.leg0, R8.Pin_1
  N16: PlayerButton-Bs.leg0, R10.Pin_1
  N17: PlayerButton-Ps.leg0, R12.Pin_1
  N18: BoxButton-S.leg0, R16.Pin_1, R17.Pin_0
  N19: BoxButton-R.leg0, R17.Pin_1, R18.Pin_0
  N20: BoxButton-Q.leg0, R18.Pin_1, R19.Pin_0
  N21: BoxButton-N.leg0, R19.Pin_1, R20.Pin_0
  N22: BoxButton-Space.leg0, R20.Pin_1
  N23: BoxButton-A.leg1, R14.Pin_1

notes:
  YDKJ Box
  -BPM 2016.11

custom parts:
  Arcade Button (white): Adafruit Arcade Button (white)
